// Logisim project cpu.circ as structural Verilog: 3 circuits, main circuit main
module main (
  input  [31:0] INSTRUCTION,
  input  CLOCK,
  output [31:0] FETCH_ADDRESS,
  output [31:0] s0_Value,
  output [31:0] s1_Value,
  output [31:0] s2_Value,
  output [31:0] ra_Value,
  output [31:0] sp_Value
);

  wire ALUSrc, and_1_out, and_2_out, BEQ, BNE, comparator_2_eq, comparator_3_eq, comparator_5_eq,
       comparator_6_eq, comparator_7_eq, comparator_8_eq, comparator_9_eq, comparator_10_eq, Jump, Link,
       Logical, lui, MemtoReg, MemWrite, mfhi, mflo, mult, PCSrc, RegDst, RegWrite, Shift, use_jr, Zero;
  wire [3:0] ALUControl;
  wire [4:0] multiplexer_1_out, multiplexer_4_out;
  wire [31:0] adder_1_out, adder_2_out, adder_3_out, aluX, aluY, bit_extender_1_out, bit_extender_2_out, hi,
       imm, lo, main_1_read_data_1, main_1_read_data_2, main_2_result, main_3_p5, multiplexer_2_out,
       multiplexer_3_out, multiplexer_6_out, multiplexer_9_out, multiplexer_10_out, multiplexer_11_out,
       multiplexer_12_out, multiplexer_13_out, multiplier_1_cout, multiplier_1_out, shamt, shifter_1_out,
       shifter_2_out, ui;

  Adder #(.width(32)) adder_1 (.a(FETCH_ADDRESS), .b(32'h4), .out(adder_1_out));  // open: cin, cout
  Shifter #(.width(32)) shifter_1 (.in(imm), .\dist (5'b00010), .out(shifter_1_out));
  Shifter #(.width(32)) shifter_2 (.in(INSTRUCTION), .\dist (5'b00010), .out(shifter_2_out));
  Adder #(.width(32)) adder_2 (.a(adder_1_out), .b(shifter_1_out), .out(adder_2_out));  // open: cin, cout
  Multiplexer #(.width(5), .enable("false")) multiplexer_1 (
    .in0(INSTRUCTION[20:16]), .in1(INSTRUCTION[15:11]), .out(multiplexer_1_out), .sel(RegDst));
  Multiplexer #(.width(32), .enable("false")) multiplexer_2 (
    .in0(adder_1_out), .in1(adder_2_out), .out(multiplexer_2_out), .sel(PCSrc));
  Multiplexer #(.width(32), .enable("false")) multiplexer_3 (
    .in0({adder_1_out[31:28], shifter_2_out[27:0]}), .in1(aluX), .out(multiplexer_3_out), .sel(use_jr));
  Multiplexer #(.width(5), .enable("false")) multiplexer_4 (
    .in0(multiplexer_1_out), .in1({5{1'b1}}), .out(multiplexer_4_out), .sel(Link));
  assign bit_extender_1_out = {{16{INSTRUCTION[15]}}, INSTRUCTION[15:0]};  // Bit_Extender bit_extender_1
  Multiplexer #(.width(32), .enable("false")) multiplexer_5 (
    .in0(bit_extender_1_out), .in1(bit_extender_2_out), .out(imm), .sel(Logical));
  assign bit_extender_2_out = {{16{1'b0}}, INSTRUCTION[15:0]};  // Bit_Extender bit_extender_2
  assign shamt = {{27{1'b0}}, INSTRUCTION[10:6]};  // Bit_Extender bit_extender_3
  Multiplexer #(.width(32), .enable("false")) multiplexer_6 (
    .in0(multiplexer_2_out), .in1(multiplexer_3_out), .out(multiplexer_6_out), .sel(Jump));
  regfile_main main_1 (
    .Read_Register_1(INSTRUCTION[25:21]), .Read_Register_2(INSTRUCTION[20:16]),
    .Write_Register(multiplexer_4_out), .Write_Data(multiplexer_9_out), .Write_Enable(RegWrite),
    .Clock(CLOCK), .Read_Data_1(main_1_read_data_1), .Read_Data_2(main_1_read_data_2), .s0_Value(s0_Value),
    .s1_Value(s1_Value), .s2_Value(s2_Value), .ra_Value(ra_Value), .sp_Value(sp_Value));
  Register #(.width(32)) PC (.D(multiplexer_6_out), .Q(FETCH_ADDRESS), .clk(CLOCK));  // open: en, clr
  Multiplexer #(.width(32), .enable("false")) multiplexer_7 (
    .in0(main_1_read_data_2), .in1(imm), .out(aluY), .sel(ALUSrc));
  Multiplexer #(.width(32), .enable("false")) multiplexer_8 (
    .in0(main_1_read_data_1), .in1(shamt), .out(aluX), .sel(Shift));
  and and_1 (and_1_out, BEQ, Zero);
  or or_1 (PCSrc, and_1_out, and_2_out);
  and and_2 (and_2_out, BNE, ~Zero);  // AND_Gate
  Comparator #(.width(6)) comparator_1 (.a(INSTRUCTION[31:26]), .b(6'b000011), .eq(Link));  // open: gt, lt
  Comparator #(.width(6)) comparator_2 (.a(INSTRUCTION[31:26]), .b({6{1'b0}}), .eq(comparator_2_eq));  // open: gt, lt
  and and_3 (use_jr, comparator_2_eq, comparator_3_eq);
  Comparator #(.width(6)) comparator_3 (.a(INSTRUCTION[5:0]), .b(6'b001000), .eq(comparator_3_eq));  // open: gt, lt
  Comparator #(.width(6)) comparator_4 (.a(INSTRUCTION[31:26]), .b(6'b001111), .eq(lui));  // open: gt, lt
  Shifter #(.width(32)) shifter_3 (.in(imm), .\dist (5'b10000), .out(ui));
  Control_Unit control_unit_1 (
    .RegDst(RegDst), .ALUControl(ALUControl), .Funct(INSTRUCTION[5:0]), .Opcode(INSTRUCTION[31:26]),
    .BEQ(BEQ), .ALUSrc(ALUSrc), .RegWrite(RegWrite), .MemToReg(MemtoReg), .MemWrite(MemWrite), .Shift(Shift),
    .Jump(Jump), .Logical(Logical), .BNE(BNE));
  alu_main main_2 (
    .Switch(ALUControl), .X(aluX), .Equal(Zero), .Result(main_2_result), .Y(aluY));  // open: Signed_Overflow
  Multiplexer #(.width(32), .enable("false")) multiplexer_9 (
    .in0(multiplexer_10_out), .in1(hi), .out(multiplexer_9_out), .sel(mfhi));
  Multiplexer #(.width(32), .enable("false")) multiplexer_10 (
    .in0(multiplexer_11_out), .in1(lo), .out(multiplexer_10_out), .sel(mflo));
  Multiplier #(.width(32)) multiplier_1 (
    .a(aluX), .b(aluY), .out(multiplier_1_out), .cout(multiplier_1_cout));  // open: cin
  Multiplexer #(.width(32), .enable("false")) multiplexer_11 (
    .in0(multiplexer_12_out), .in1(ui), .out(multiplexer_11_out), .sel(lui));
  Register #(.width(32)) u_Lo (.D(multiplier_1_out), .en(mult), .Q(lo), .clk(CLOCK));  // open: clr
  Register #(.width(32)) u_Hi (.D(multiplier_1_cout), .en(mult), .Q(hi), .clk(CLOCK));  // open: clr
  // Probe on INSTRUCTION[31:26]
  // Probe on INSTRUCTION[5:0]
  // Probe on INSTRUCTION[25:21]
  // Probe on INSTRUCTION[20:16]
  // Probe on INSTRUCTION[15:11]
  // Probe on shamt
  // Probe on imm
  // mem_main main_3: pin names not known; wires that end beside it: main_2_result, main_1_read_data_2, MemWrite, CLOCK, main_3_p5
  Multiplexer #(.width(32), .enable("false")) multiplexer_12 (
    .in0(multiplexer_13_out), .in1(adder_3_out), .out(multiplexer_12_out), .sel(Link));
  Multiplexer #(.width(32), .enable("false")) multiplexer_13 (
    .in0(main_2_result), .in1(main_3_p5), .out(multiplexer_13_out), .sel(MemtoReg));
  Adder #(.width(32)) adder_3 (.a(FETCH_ADDRESS), .b(32'h4), .out(adder_3_out));  // open: cin, cout
  // Probe on s0_Value
  // Probe on s1_Value
  // Probe on s2_Value
  // Probe on ra_Value
  // Probe on sp_Value
  // Probe on ALUControl
  Comparator #(.width(6)) comparator_5 (.a(INSTRUCTION[31:26]), .b({6{1'b0}}), .eq(comparator_5_eq));  // open: gt, lt
  and and_4 (mult, comparator_5_eq, comparator_6_eq);
  Comparator #(.width(6)) comparator_6 (.a(INSTRUCTION[5:0]), .b(6'b011000), .eq(comparator_6_eq));  // open: gt, lt
  Comparator #(.width(6)) comparator_7 (.a(INSTRUCTION[31:26]), .b({6{1'b0}}), .eq(comparator_7_eq));  // open: gt, lt
  and and_5 (mflo, comparator_7_eq, comparator_8_eq);
  Comparator #(.width(6)) comparator_8 (.a(INSTRUCTION[5:0]), .b(6'b010010), .eq(comparator_8_eq));  // open: gt, lt
  Comparator #(.width(6)) comparator_9 (.a(INSTRUCTION[31:26]), .b({6{1'b0}}), .eq(comparator_9_eq));  // open: gt, lt
  and and_6 (mfhi, comparator_9_eq, comparator_10_eq);
  Comparator #(.width(6)) comparator_10 (.a(INSTRUCTION[5:0]), .b(6'b010000), .eq(comparator_10_eq));  // open: gt, lt
  // Probe on aluX
  // Probe on aluY

  // Other names for the same wires on the sheet: clk = CLOCK; fetch_addr[31:0] = FETCH_ADDRESS;
  //   funct[5:0] = INSTRUCTION[5:0]; rd[4:0] = INSTRUCTION[15:11]; rt[4:0] = INSTRUCTION[20:16];
  //   rs[4:0] = INSTRUCTION[25:21]; opcode[5:0] = INSTRUCTION[31:26]; ra[31:0] = ra_Value; s0[31:0] = s0_Value;
  //   s1[31:0] = s1_Value; s2[31:0] = s2_Value; sp[31:0] = sp_Value

  // Notes on the sheet:
  //   Output
  //   These are outputs/inputs from run.circ
  //   Instruction Decoder
  //   Inputs
  //   PC Control
  //   Miscellaneous
  //   BEQ or BNE
  //   LUI
  //   Single-cycle MIPS Datapath
  //   JAL
  //   JR
  //   These are DEBUG/TEST outputs from your circuit.
  //   Control Unit
  //   Multiplication Unit
  //   For Debugging Purposes Only
endmodule

module Control_Unit (
  input  [5:0] Opcode,
  input  [5:0] Funct,
  output RegDst,
  output RegWrite,
  output MemWrite,
  output MemToReg,
  output ALUSrc,
  output BEQ,
  output BNE,
  output Jump,
  output Logical,
  output Shift,
  output [3:0] ALUControl
);

  wire add, addi, addiu, addu, \and , andi, beq_t, bne_t, comparator_15_eq, comparator_16_eq,
       comparator_17_eq, comparator_18_eq, comparator_19_eq, comparator_20_eq, comparator_21_eq,
       comparator_22_eq, comparator_23_eq, comparator_24_eq, comparator_25_eq, comparator_26_eq,
       comparator_27_eq, j, jal, jr, lui, lw, Main_Decoder_jump, mfhi, mflo, mult, \or , or_2_out, or_4_out,
       or_5_out, or_6_out, or_7_out, or_8_out, or_9_out, ori, Rtype, sll, slt, slti, sltiu, sltu, sra, srl,
       sw;
  wire [3:0] multiplexer_1_out, multiplexer_2_out, multiplexer_3_out, multiplexer_4_out, multiplexer_5_out,
       multiplexer_6_out, multiplexer_7_out, multiplexer_8_out, multiplexer_9_out, multiplexer_10_out,
       multiplexer_11_out, multiplexer_12_out, multiplexer_13_out, multiplexer_14_out, multiplexer_15_out;

  Main_Decoder Main_Decoder (
    .opcode5(Opcode[5]), .opcode4(Opcode[4]), .opcode3(Opcode[3]), .opcode2(Opcode[2]), .opcode1(Opcode[1]),
    .opcode0(Opcode[0]), .RegDst(RegDst), .ALUSrc(ALUSrc), .MemToReg(MemToReg), .BEQ(BEQ),
    .Jump(Main_Decoder_jump), .RegWrite(RegWrite), .MemWrite(MemWrite), .Logical(Logical), .BNE(BNE));
  Comparator #(.width(6)) comparator_1 (.a(Opcode), .b({6{1'b0}}), .eq(Rtype));  // open: gt, lt
  or or_1 (Shift, sll, srl, sra);
  or or_2 (or_2_out, sltu, sltiu);
  or or_3 (Jump, Main_Decoder_jump, jr);
  Multiplexer #(.width(4), .enable("false")) multiplexer_1 (
    .in0(4'b0000), .in1(4'b1111), .out(multiplexer_1_out), .sel(or_2_out));
  or or_4 (or_4_out, slt, slti);
  Multiplexer #(.width(4), .enable("false")) multiplexer_2 (
    .in0(multiplexer_15_out), .in1(4'b0111), .out(multiplexer_2_out), .sel(1'b0));
  or or_5 (or_5_out, beq_t, bne_t);
  Multiplexer #(.width(4), .enable("false")) multiplexer_3 (
    .in0(multiplexer_1_out), .in1(4'b1110), .out(multiplexer_3_out), .sel(or_4_out));
  Multiplexer #(.width(4), .enable("false")) multiplexer_4 (
    .in0(multiplexer_2_out), .in1(4'b0110), .out(multiplexer_4_out), .sel(or_5_out));
  Multiplexer #(.width(4), .enable("false")) multiplexer_5 (
    .in0(multiplexer_3_out), .in1(4'b1101), .out(multiplexer_5_out), .sel(1'b0));
  Multiplexer #(.width(4), .enable("false")) multiplexer_6 (
    .in0(multiplexer_4_out), .in1(4'b0101), .out(multiplexer_6_out), .sel(1'b0));
  or or_6 (or_6_out, addu, addiu);
  Comparator #(.width(6)) comparator_2 (.a(Opcode), .b(6'b001001), .eq(addiu));  // open: gt, lt
  Comparator #(.width(6)) comparator_3 (.a(Opcode), .b(6'b001000), .eq(addi));  // open: gt, lt
  Comparator #(.width(6)) comparator_4 (.a(Opcode), .b(6'b000011), .eq(jal));  // open: gt, lt
  Comparator #(.width(6)) comparator_5 (.a(Opcode), .b(6'b000010), .eq(j));  // open: gt, lt
  Comparator #(.width(6)) comparator_6 (.a(Opcode), .b(6'b001011), .eq(sltiu));  // open: gt, lt
  Comparator #(.width(6)) comparator_7 (.a(Opcode), .b(6'b001010), .eq(slti));  // open: gt, lt
  Comparator #(.width(6)) comparator_8 (.a(Opcode), .b(6'b001100), .eq(andi));  // open: gt, lt
  Comparator #(.width(6)) comparator_9 (.a(Opcode), .b(6'b001101), .eq(ori));  // open: gt, lt
  Comparator #(.width(6)) comparator_10 (.a(Opcode), .b(6'b001111), .eq(lui));  // open: gt, lt
  Comparator #(.width(6)) comparator_11 (.a(Opcode), .b(6'b100011), .eq(lw));  // open: gt, lt
  Comparator #(.width(6)) comparator_12 (.a(Opcode), .b(6'b101011), .eq(sw));  // open: gt, lt
  Comparator #(.width(6)) comparator_13 (.a(Opcode), .b(6'b000100), .eq(beq_t));  // open: gt, lt
  Comparator #(.width(6)) comparator_14 (.a(Opcode), .b(6'b000101), .eq(bne_t));  // open: gt, lt
  Multiplexer #(.width(4), .enable("false")) multiplexer_7 (
    .in0(multiplexer_5_out), .in1(4'b1100), .out(multiplexer_7_out), .sel(1'b0));
  or or_7 (or_7_out, \or , ori);
  Multiplexer #(.width(4), .enable("false")) multiplexer_8 (
    .in0(multiplexer_6_out), .in1(4'b0100), .out(multiplexer_8_out), .sel(or_6_out));
  or or_8 (or_8_out, add, lw, sw, addi);
  Multiplexer #(.width(4), .enable("false")) multiplexer_9 (
    .in0(multiplexer_7_out), .in1(4'b1011), .out(multiplexer_9_out), .sel(or_7_out));
  or or_9 (or_9_out, \and , andi);
  Multiplexer #(.width(4), .enable("false")) multiplexer_10 (
    .in0(multiplexer_8_out), .in1(4'b0011), .out(multiplexer_10_out), .sel(or_8_out));
  Comparator #(.width(6)) comparator_15 (.a(Funct), .b({6{1'b0}}), .eq(comparator_15_eq));  // open: gt, lt
  Comparator #(.width(6)) comparator_16 (.a(Funct), .b(6'b000010), .eq(comparator_16_eq));  // open: gt, lt
  Comparator #(.width(6)) comparator_17 (.a(Funct), .b(6'b000011), .eq(comparator_17_eq));  // open: gt, lt
  Comparator #(.width(6)) comparator_18 (.a(Funct), .b(6'b100000), .eq(comparator_18_eq));  // open: gt, lt
  Comparator #(.width(6)) comparator_19 (.a(Funct), .b(6'b100001), .eq(comparator_19_eq));  // open: gt, lt
  Comparator #(.width(6)) comparator_20 (.a(Funct), .b(6'b001000), .eq(comparator_20_eq));  // open: gt, lt
  Comparator #(.width(6)) comparator_21 (.a(Funct), .b(6'b101010), .eq(comparator_21_eq));  // open: gt, lt
  Comparator #(.width(6)) comparator_22 (.a(Funct), .b(6'b101011), .eq(comparator_22_eq));  // open: gt, lt
  Comparator #(.width(6)) comparator_23 (.a(Funct), .b(6'b100100), .eq(comparator_23_eq));  // open: gt, lt
  Comparator #(.width(6)) comparator_24 (.a(Funct), .b(6'b100101), .eq(comparator_24_eq));  // open: gt, lt
  Comparator #(.width(6)) comparator_25 (.a(Funct), .b(6'b011000), .eq(comparator_25_eq));  // open: gt, lt
  Comparator #(.width(6)) comparator_26 (.a(Funct), .b(6'b010010), .eq(comparator_26_eq));  // open: gt, lt
  Comparator #(.width(6)) comparator_27 (.a(Funct), .b(6'b010000), .eq(comparator_27_eq));  // open: gt, lt
  Multiplexer #(.width(4), .enable("false")) multiplexer_11 (
    .in0(multiplexer_9_out), .in1(4'b1010), .out(multiplexer_11_out), .sel(or_9_out));
  Multiplexer #(.width(4), .enable("false")) multiplexer_12 (
    .in0(multiplexer_10_out), .in1(4'b0010), .out(multiplexer_12_out), .sel(sra));
  Multiplexer #(.width(4), .enable("false")) multiplexer_13 (
    .in0(multiplexer_11_out), .in1(4'b1001), .out(multiplexer_13_out), .sel(1'b0));
  Multiplexer #(.width(4), .enable("false")) multiplexer_14 (
    .in0(multiplexer_12_out), .in1(4'b0001), .out(multiplexer_14_out), .sel(srl));
  and and_1 (sll, comparator_15_eq, Rtype);
  and and_2 (srl, comparator_16_eq, Rtype);
  and and_3 (sra, comparator_17_eq, Rtype);
  and and_4 (add, comparator_18_eq, Rtype);
  and and_5 (addu, comparator_19_eq, Rtype);
  and and_6 (jr, comparator_20_eq, Rtype);
  and and_7 (slt, comparator_21_eq, Rtype);
  and and_8 (sltu, comparator_22_eq, Rtype);
  and and_9 (\and , comparator_23_eq, Rtype);
  and and_10 (\or , comparator_24_eq, Rtype);
  and and_11 (mult, comparator_25_eq, Rtype);
  and and_12 (mflo, comparator_26_eq, Rtype);
  and and_13 (mfhi, comparator_27_eq, Rtype);
  Multiplexer #(.width(4), .enable("false")) multiplexer_15 (
    .in0(multiplexer_13_out), .in1(4'b1000), .out(multiplexer_15_out), .sel(1'b0));
  Multiplexer #(.width(4), .enable("false")) multiplexer_16 (
    .in0(multiplexer_14_out), .in1(4'b0000), .out(ALUControl), .sel(sll));

  // Notes on the sheet:
  //   Alu Decoder
  //   Supports only operations from ALU
  //   Other
  //   All Project 2-2 instructions
  //   R-Type
  //   Operations not supported by ALU
endmodule

module Main_Decoder (
  input  opcode5,
  input  opcode4,
  input  opcode3,
  input  opcode2,
  input  opcode1,
  input  opcode0,
  output RegDst,
  output RegWrite,
  output MemToReg,
  output MemWrite,
  output ALUSrc,
  output BEQ,
  output BNE,
  output Jump,
  output Logical
);

  wire addi_out, addiu_out, andi_out, jal_out, jump_out, lui_out, lw_out, ori_out, slti_out, sltiu_out;

  and R_Type (RegDst, ~opcode5, ~opcode4, ~opcode3, ~opcode2, ~opcode1, ~opcode0);  // AND_Gate
  and lw (lw_out, opcode5, ~opcode4, ~opcode3, ~opcode2, opcode1, opcode0);  // AND_Gate
  and sw (MemWrite, opcode5, ~opcode4, opcode3, ~opcode2, opcode1, opcode0);  // AND_Gate
  and u_beq (BEQ, ~opcode5, ~opcode4, ~opcode3, opcode2, ~opcode1, ~opcode0);  // AND_Gate
  and u_bne (BNE, ~opcode5, ~opcode4, ~opcode3, opcode2, ~opcode1, opcode0);  // AND_Gate
  and u_jump (jump_out, ~opcode5, ~opcode4, ~opcode3, ~opcode2, opcode1, ~opcode0);  // AND_Gate
  and jal (jal_out, ~opcode5, ~opcode4, ~opcode3, ~opcode2, opcode1, opcode0);  // AND_Gate
  and addi (addi_out, ~opcode5, ~opcode4, opcode3, ~opcode2, ~opcode1, ~opcode0);  // AND_Gate
  and addiu (addiu_out, ~opcode5, ~opcode4, opcode3, ~opcode2, ~opcode1, opcode0);  // AND_Gate
  and slti (slti_out, ~opcode5, ~opcode4, opcode3, ~opcode2, opcode1, ~opcode0);  // AND_Gate
  and sltiu (sltiu_out, ~opcode5, ~opcode4, opcode3, ~opcode2, opcode1, opcode0);  // AND_Gate
  and andi (andi_out, ~opcode5, ~opcode4, opcode3, opcode2, ~opcode1, ~opcode0);  // AND_Gate
  and ori (ori_out, ~opcode5, ~opcode4, opcode3, opcode2, ~opcode1, opcode0);  // AND_Gate
  and lui (lui_out, ~opcode5, ~opcode4, opcode3, opcode2, opcode1, opcode0);  // AND_Gate
  or or_1 (RegWrite, RegDst, lw_out, jal_out, addi_out, addiu_out, slti_out, sltiu_out, andi_out, ori_out, lui_out);
  or or_2 (MemToReg, lw_out, jal_out);
  or or_3 (ALUSrc, lw_out, MemWrite, addi_out, addiu_out, slti_out, sltiu_out, andi_out, ori_out, lui_out);
  or or_4 (Jump, jump_out, jal_out);
  or or_5 (Logical, andi_out, ori_out);
endmodule
