// Logisim project extra_hex_io.circ as structural Verilog: 1 circuit, main circuit main
module main (
  output [31:0] s0_Value,
  output [31:0] s1_Value,
  output [31:0] s2_Value,
  output [31:0] ra_Value,
  output [31:0] sp_Value,
  output [31:0] Time_Step,
  output [31:0] Requested_Address,
  output [31:0] Requested_Instruction,
  output halt
);

  wire clock_1_out;

  Clock clock_1 (.out(clock_1_out));
  cpu_main main_1 (
    .INSTRUCTION(Requested_Instruction), .CLOCK(clock_1_out), .FETCH_ADDRESS(Requested_Address),
    .s0_Value(s0_Value), .s1_Value(s1_Value), .s2_Value(s2_Value), .ra_Value(ra_Value), .sp_Value(sp_Value));
  Counter #(.width(32), .max('hffffffff)) counter_1 (
    .Q(Time_Step), .clk(clock_1_out));  // open: load, D, count, carry, clr
  Comparator #(.width(32)) comparator_1 (.a(Time_Step), .b(32'h12), .eq(halt));  // open: gt, lt
  Hex_Digit_Display hex_digit_display_1 (.value(s0_Value[31:28]));  // open: dp
  // Probe on s0_Value
  Hex_Digit_Display hex_digit_display_2 (.value(s0_Value[23:20]));  // open: dp
  Hex_Digit_Display hex_digit_display_3 (.value(s0_Value[27:24]));  // open: dp
  // Probe on Requested_Address
  Hex_Digit_Display hex_digit_display_4 (.value(s0_Value[19:16]));  // open: dp
  Hex_Digit_Display hex_digit_display_5 (.value(s0_Value[11:8]));  // open: dp
  Hex_Digit_Display hex_digit_display_6 (.value(s0_Value[15:12]));  // open: dp
  Hex_Digit_Display hex_digit_display_7 (.value(s0_Value[7:4]));  // open: dp
  ROM #(.addrWidth(24), .dataWidth(32)) rom_1 (
    .addr(Requested_Address[25:2]), .data(Requested_Instruction));  // open: sel
  Hex_Digit_Display hex_digit_display_8 (.value(s0_Value[3:0]));  // open: dp
  // Probe on Requested_Instruction

  // Other names for the same wires on the sheet: fetch_addr[31:0] = Requested_Address;
  //   Instruction[31:0] = Requested_Instruction

  // Notes on the sheet:
  //   YOUR CPU SHOULD FIT IN HERE!
  //   Binary to Hex
  //   Instruction Memory
  //   contents of rom_1 (hex, n*v repeats v):
  //   3c0100c0 3421ffee 18021 3c010000 3421f00d 18021 24100bed 3c01000a 3421d0be 18021 24100dab 3c01ba5e
  //   3421ba11 18021 3c010000 3421dead 18021
endmodule
