// Logisim project simple_io.circ as structural Verilog: 1 circuit, main circuit main
module main (
  output [31:0] s0_Value,
  output [31:0] s1_Value,
  output [31:0] s2_Value,
  output [31:0] ra_Value,
  output [31:0] sp_Value,
  output [31:0] Time_Step,
  output [31:0] Requested_Address,
  output [31:0] Requested_Instruction,
  output halt
);

  wire clock_1_out, comparator_1_eq, comparator_2_eq;

  Clock clock_1 (.out(clock_1_out));
  cpu_main main_1 (
    .INSTRUCTION(Requested_Instruction), .CLOCK(clock_1_out), .FETCH_ADDRESS(Requested_Address),
    .s0_Value(s0_Value), .s1_Value(s1_Value), .s2_Value(s2_Value), .ra_Value(ra_Value), .sp_Value(sp_Value));
  Counter #(.width(32), .max('hffffffff)) counter_1 (
    .Q(Time_Step), .clk(clock_1_out));  // open: load, D, count, carry, clr
  Comparator #(.width(32)) comparator_1 (.a(s0_Value), .b(32'h1), .eq(comparator_1_eq));  // open: gt, lt
  Comparator #(.width(32)) comparator_2 (.a(s1_Value), .b(32'h1), .eq(comparator_2_eq));  // open: gt, lt
  Comparator #(.width(32)) comparator_3 (.a(Time_Step), .b(32'h7), .eq(halt));  // open: gt, lt
  LED Value_at_0x00007F00 (.in(comparator_1_eq));
  LED Value_at_0x00007F04 (.in(comparator_2_eq));
  // Probe on Requested_Address
  ROM #(.addrWidth(24), .dataWidth(32)) rom_1 (
    .addr(Requested_Address[25:2]), .data(Requested_Instruction));  // open: sel
  // Probe on Requested_Instruction

  // Other names for the same wires on the sheet: fetch_addr[31:0] = Requested_Address;
  //   Instruction[31:0] = Requested_Instruction

  // Notes on the sheet:
  //   YOUR CPU SHOULD FIT IN HERE!
  //   Instruction Memory
  //   contents of rom_1 (hex, n*v repeats v):
  //   24080001 24097f00 ad280000 ad280004 8d300000 8d310004
endmodule
