// Logisim project test_comparison.circ as structural Verilog: 1 circuit, main circuit main
module main (
  output [31:0] s0_Value,
  output [31:0] s1_Value,
  output [31:0] s2_Value,
  output [31:0] sp_Value,
  output halt
);

  wire clock_1_out;
  wire [31:0] counter_1_q, fetch_addr, Instruction, main_1_ra_value;

  Clock clock_1 (.out(clock_1_out));
  cpu_main main_1 (
    .INSTRUCTION(Instruction), .CLOCK(clock_1_out), .FETCH_ADDRESS(fetch_addr), .s0_Value(s0_Value),
    .s1_Value(s1_Value), .s2_Value(s2_Value), .ra_Value(main_1_ra_value), .sp_Value(sp_Value));
  Counter #(.width(32), .max('hffffffff)) counter_1 (
    .Q(counter_1_q), .clk(clock_1_out));  // open: load, D, count, carry, clr
  Comparator #(.width(32)) comparator_1 (.a(counter_1_q), .b(32'h13), .eq(halt));  // open: gt, lt
  // Probe on fetch_addr
  ROM #(.addrWidth(24), .dataWidth(32)) rom_1 (.addr(fetch_addr[25:2]), .data(Instruction));  // open: sel
  // Probe on Instruction

  // Notes on the sheet:
  //   YOUR CPU SHOULD FIT IN HERE!
  //   Instruction Memory
  //   contents of rom_1 (hex, n*v repeats v):
  //   20100001 2011fffe 211902a 230902a 230902b 211902b 2e120000 2e320000 2e120002 2e320002 2e12fffd
  //   2e32fffd 2a120000 2a320000 2a120002 2a320002 2a12fffd 2a32fffd
endmodule
