// Logisim project test_jump.circ as structural Verilog: 1 circuit, main circuit main
module main (
  output [31:0] s0_Value,
  output [31:0] s1_Value,
  output [31:0] s2_Value,
  output [31:0] ra_Value,
  output [31:0] sp_Value,
  output [31:0] Time_Step,
  output halt
);

  wire clock_1_out;
  wire [31:0] fetch_addr, Instruction;

  Clock clock_1 (.out(clock_1_out));
  cpu_main main_1 (
    .INSTRUCTION(Instruction), .CLOCK(clock_1_out), .FETCH_ADDRESS(fetch_addr), .s0_Value(s0_Value),
    .s1_Value(s1_Value), .s2_Value(s2_Value), .ra_Value(ra_Value), .sp_Value(sp_Value));
  Counter #(.width(32), .max('hffffffff)) counter_1 (
    .Q(Time_Step), .clk(clock_1_out));  // open: load, D, count, carry, clr
  Comparator #(.width(32)) comparator_1 (.a(Time_Step), .b(32'hf), .eq(halt));  // open: gt, lt
  // Probe on fetch_addr
  ROM #(.addrWidth(24), .dataWidth(32)) rom_1 (.addr(fetch_addr[25:2]), .data(Instruction));  // open: sel
  // Probe on Instruction

  // Notes on the sheet:
  //   YOUR CPU SHOULD FIT IN HERE!
  //   Instruction Memory
  //   contents of rom_1 (hex, n*v repeats v):
  //   8000008 2118820 c000006 800000c 26110006 3e00008 2118820 3e00008 20100005 c000004 2118820 8000001
  //   2231ffe6 2210fffb
endmodule
